// Digital circuit pong.dig as structural Verilog
module pong (
  input  Master_VGA_Clock,
  input  in_2,
  input  in_3,
  input  in_4,
  input  in_5,
  input  Test_Clock,
  input  in_7,
  input  in_8,
  input  Manual_Clock
);

  wire _7400_1_pin4, _7400_1_pin5, _7408_1_pin3, _7408_1_pin6, _7408_1_pin8, _7408_1_pin11, _7408_1_pin12,
       _7408_2_pin3, _7408_2_pin6, _7408_2_pin8, _7408_2_pin11, _7408_3_pin3, _7408_3_pin4, _7408_3_pin5,
       _7408_3_pin6, _7408_4_pin2, _7408_4_pin3, _7408_4_pin4, _7408_4_pin5, _7408_4_pin6, _7408_4_pin8,
       _7408_4_pin11, _7408_4_pin12, _7408_4_pin13, _7408_5_pin1, _7408_5_pin2, _7408_5_pin3, _7408_5_pin6,
       _7485_1_pin5, _7485_1_pin6, _7485_1_pin7, _7485_2_pin5, _7485_2_pin6, _7485_2_pin7, _7485_3_pin7,
       _7485_4_pin5, _7485_4_pin6, _7485_4_pin7, _7485_5_pin5, _7485_5_pin6, _7485_5_pin7, _7485_6_pin5,
       _7485_7_pin5, _7485_7_pin6, _7485_7_pin7, _7485_8_pin5, _7485_8_pin6, _7485_8_pin7, _7485_10_pin5,
       _7485_10_pin6, _7485_10_pin7, _7485_11_pin5, _7485_11_pin6, _7485_11_pin7, _74163_1_pin15,
       _74163_2_pin15, _74163_4_pin15, _74163_5_pin15, and_1_out, and_2_out, CLK, comparator_1_gt,
       comparator_2_lt, comparator_3_gt, comparator_4_lt, H0, H1, H2, H3, H4, H5, H6, H7, H8, H9, H10, H11,
       HCLR, HSYNC, not_1_out, not_2_out, not_3_out, not_4_out, V0, V1, V2, V3, V4, V5, V6, V7, V8, V9, V10,
       V11, VCLR, VSYNC;

  // Probe on {H9, H8, H7, H6, H5, H4, H3, H2, H1, H0}
  // Probe on {V9, V8, V7, V6, V5, V4, V3, V2, V1, V0}
  Comparator #(.Bits(10)) comparator_1 (
    .a({H9, H8, H7, H6, H5, H4, H3, H2, H1, H0}), .b(10'h28f), .gt(comparator_1_gt));  // open: eq, lt
  Comparator #(.Bits(10)) comparator_2 (
    .a({H9, H8, H7, H6, H5, H4, H3, H2, H1, H0}), .b(10'h2f0), .lt(comparator_2_lt));  // open: gt, eq
  Comparator #(.Bits(10)) comparator_3 (
    .a({V9, V8, V7, V6, V5, V4, V3, V2, V1, V0}), .b(10'h1e8), .gt(comparator_3_gt));  // open: eq, lt
  Comparator #(.Bits(10)) comparator_4 (
    .a({V9, V8, V7, V6, V5, V4, V3, V2, V1, V0}), .b(10'h1eb), .lt(comparator_4_lt));  // open: gt, eq
  and and_1 (and_1_out, comparator_1_gt, comparator_2_lt);
  and and_2 (and_2_out, comparator_3_gt, comparator_4_lt);
  not not_1 (not_1_out, and_1_out);
  not not_2 (not_2_out, and_2_out);
  Switch switch_1 (.A(not_1_out), .B(HSYNC));
  Switch switch_2 (.A(not_2_out), .B(VSYNC));
  _74163 _74163_1 (
    .pin1(HCLR), .pin2(CLK), .pin3(1'b0), .pin4(1'b0), .pin5(1'b0), .pin6(1'b0), .pin7(1'b1), .pin8(1'b0),
    .pin9(1'b1), .pin10(1'b1), .pin11(H3), .pin12(H2), .pin13(H1), .pin14(H0), .pin15(_74163_1_pin15),
    .pin16(1'b1));
  _74163 _74163_2 (
    .pin1(HCLR), .pin2(CLK), .pin3(1'b0), .pin4(1'b0), .pin5(1'b0), .pin6(1'b0), .pin7(1'b1), .pin8(1'b0),
    .pin9(1'b1), .pin10(_74163_1_pin15), .pin11(H7), .pin12(H6), .pin13(H5), .pin14(H4),
    .pin15(_74163_2_pin15), .pin16(1'b1));
  _74163 _74163_3 (
    .pin1(HCLR), .pin2(CLK), .pin3(1'b0), .pin4(1'b0), .pin5(1'b0), .pin6(1'b0), .pin7(1'b1), .pin8(1'b0),
    .pin9(1'b1), .pin10(_74163_2_pin15), .pin11(H11), .pin12(H10), .pin13(H9), .pin14(H8), .pin16(1'b1));  // open: pin15
  _74163 _74163_4 (
    .pin1(VCLR), .pin2(HCLR), .pin3(1'b0), .pin4(1'b0), .pin5(1'b0), .pin6(1'b0), .pin7(1'b1), .pin8(1'b0),
    .pin9(1'b1), .pin10(1'b1), .pin11(V3), .pin12(V2), .pin13(V1), .pin14(V0), .pin15(_74163_4_pin15),
    .pin16(1'b1));
  _74163 _74163_5 (
    .pin1(VCLR), .pin2(HCLR), .pin3(1'b0), .pin4(1'b0), .pin5(1'b0), .pin6(1'b0), .pin7(1'b1), .pin8(1'b0),
    .pin9(1'b1), .pin10(_74163_4_pin15), .pin11(V7), .pin12(V6), .pin13(V5), .pin14(V4),
    .pin15(_74163_5_pin15), .pin16(1'b1));
  _74163 _74163_6 (
    .pin1(VCLR), .pin2(HCLR), .pin3(1'b0), .pin4(1'b0), .pin5(1'b0), .pin6(1'b0), .pin7(1'b1), .pin8(1'b0),
    .pin9(1'b1), .pin10(_74163_5_pin15), .pin11(V11), .pin12(V10), .pin13(V9), .pin14(V8), .pin16(1'b1));  // open: pin15
  not not_3 (not_3_out, H7);
  not not_4 (not_4_out, H6);
  _7408 _7408_1 (
    .pin1(H9), .pin2(H8), .pin3(_7408_1_pin3), .pin4(not_3_out), .pin5(not_4_out), .pin6(_7408_1_pin6),
    .pin7(1'b0), .pin8(_7408_1_pin8), .pin9(H3), .pin10(H2), .pin11(_7408_1_pin11), .pin12(_7408_1_pin12),
    .pin13(H4), .pin14(1'b1));
  _7408 _7408_2 (
    .pin1(H1), .pin2(H0), .pin3(_7408_2_pin3), .pin4(_7408_1_pin3), .pin5(_7408_1_pin6), .pin6(_7408_2_pin6),
    .pin7(1'b0), .pin8(_7408_2_pin8), .pin9(_7408_2_pin6), .pin10(_7408_2_pin3), .pin11(_7408_2_pin11),
    .pin12(_7408_1_pin8), .pin13(_7408_1_pin11), .pin14(1'b1));
  not not_5 (_7408_1_pin12, H5);
  // Relay relay_1: pin names not known; wires that end beside it: Master_VGA_Clock, Test_Clock, in_7, in_8, CLK
  // Relay relay_2: pin names not known; wires that end beside it: Manual_Clock, CLK
  // Relay relay_3: pin names not known; wires that end beside it: in_2, 1'b0, CLK, 1'b0, 1'b0
  _7408 _7408_3 (
    .pin1(_7408_2_pin11), .pin2(_7408_2_pin8), .pin3(_7408_3_pin3), .pin4(_7408_3_pin4), .pin5(_7408_3_pin5),
    .pin6(_7408_3_pin6), .pin7(1'b0), .pin9(1'b1), .pin10(1'b1), .pin12(1'b1), .pin13(1'b1), .pin14(1'b1));  // open: pin8, pin11
  not not_6 (HCLR, _7408_3_pin3);
  not not_7 (VCLR, _7408_3_pin6);
  _7408 _7408_4 (
    .pin1(V9), .pin2(_7408_4_pin2), .pin3(_7408_4_pin3), .pin4(_7408_4_pin4), .pin5(_7408_4_pin5),
    .pin6(_7408_4_pin6), .pin7(1'b0), .pin8(_7408_4_pin8), .pin9(V3), .pin10(V2), .pin11(_7408_4_pin11),
    .pin12(_7408_4_pin12), .pin13(_7408_4_pin13), .pin14(1'b1));
  not not_8 (_7408_4_pin2, V8);
  not not_9 (_7408_4_pin4, V7);
  not not_10 (_7408_4_pin5, V6);
  _7408 _7408_5 (
    .pin1(_7408_5_pin1), .pin2(_7408_5_pin2), .pin3(_7408_5_pin3), .pin4(_7408_4_pin3), .pin5(_7408_4_pin6),
    .pin6(_7408_5_pin6), .pin7(1'b0), .pin8(_7408_3_pin5), .pin9(_7408_5_pin6), .pin10(_7408_5_pin3),
    .pin11(_7408_3_pin4), .pin12(_7408_4_pin8), .pin13(_7408_4_pin11), .pin14(1'b1));
  not not_11 (_7408_5_pin1, V1);
  not not_12 (_7408_5_pin2, V0);
  VGA vga_1 (.R(in_3), .G(in_4), .B(in_5), .H(HSYNC), .V(VSYNC), .C(CLK));
  not not_13 (_7408_4_pin13, V4);
  not not_14 (_7408_4_pin12, V5);
  _7485 _7485_1 (
    .pin1(V3), .pin2(1'b0), .pin3(1'b1), .pin4(1'b0), .pin5(_7485_1_pin5), .pin6(_7485_1_pin6),
    .pin7(_7485_1_pin7), .pin8(1'b0), .pin9(V0), .pin10(1'b0), .pin11(V1), .pin12(1'b0), .pin13(1'b0),
    .pin14(V2), .pin15(1'b1), .pin16(1'b1));
  _7485 _7485_2 (
    .pin1(V7), .pin2(_7485_1_pin7), .pin3(_7485_1_pin6), .pin4(_7485_1_pin5), .pin5(_7485_2_pin5),
    .pin6(_7485_2_pin6), .pin7(_7485_2_pin7), .pin8(1'b0), .pin9(V4), .pin10(1'b0), .pin11(V5), .pin12(1'b1),
    .pin13(1'b1), .pin14(V6), .pin15(1'b1), .pin16(1'b1));
  _7485 _7485_3 (
    .pin1(1'b0), .pin2(_7485_2_pin7), .pin3(_7485_2_pin6), .pin4(_7485_2_pin5), .pin7(_7485_3_pin7),
    .pin8(1'b0), .pin9(V8), .pin10(1'b1), .pin11(V9), .pin12(1'b0), .pin13(1'b0), .pin14(1'b0), .pin15(1'b0),
    .pin16(1'b1));  // open: pin5, pin6
  _7485 _7485_4 (
    .pin1(V3), .pin2(1'b0), .pin3(1'b1), .pin4(1'b0), .pin5(_7485_4_pin5), .pin6(_7485_4_pin6),
    .pin7(_7485_4_pin7), .pin8(1'b0), .pin9(V0), .pin10(1'b1), .pin11(V1), .pin12(1'b1), .pin13(1'b0),
    .pin14(V2), .pin15(1'b1), .pin16(1'b1));
  _7485 _7485_5 (
    .pin1(V7), .pin2(_7485_4_pin7), .pin3(_7485_4_pin6), .pin4(_7485_4_pin5), .pin5(_7485_5_pin5),
    .pin6(_7485_5_pin6), .pin7(_7485_5_pin7), .pin8(1'b0), .pin9(V4), .pin10(1'b0), .pin11(V5), .pin12(1'b1),
    .pin13(1'b1), .pin14(V6), .pin15(1'b1), .pin16(1'b1));
  _7485 _7485_6 (
    .pin1(1'b0), .pin2(_7485_5_pin7), .pin3(_7485_5_pin6), .pin4(_7485_5_pin5), .pin5(_7485_6_pin5),
    .pin8(1'b0), .pin9(V8), .pin10(1'b1), .pin11(V9), .pin12(1'b0), .pin13(1'b0), .pin14(1'b0), .pin15(1'b0),
    .pin16(1'b1));  // open: pin6, pin7
  _7400 _7400_1 (
    .pin1(_7485_3_pin7), .pin2(_7485_6_pin5), .pin3(VSYNC), .pin4(_7400_1_pin4), .pin5(_7400_1_pin5),
    .pin6(HSYNC), .pin7(1'b0), .pin9(1'b1), .pin10(1'b1), .pin12(1'b1), .pin13(1'b1), .pin14(1'b1));  // open: pin8, pin11
  _7485 _7485_7 (
    .pin1(H3), .pin2(1'b0), .pin3(1'b1), .pin4(1'b0), .pin5(_7485_7_pin5), .pin6(_7485_7_pin6),
    .pin7(_7485_7_pin7), .pin8(1'b0), .pin9(H0), .pin10(1'b1), .pin11(H1), .pin12(1'b1), .pin13(1'b1),
    .pin14(H2), .pin15(1'b1), .pin16(1'b1));
  _7485 _7485_8 (
    .pin1(H7), .pin2(_7485_7_pin7), .pin3(_7485_7_pin6), .pin4(_7485_7_pin5), .pin5(_7485_8_pin5),
    .pin6(_7485_8_pin6), .pin7(_7485_8_pin7), .pin8(1'b0), .pin9(H4), .pin10(1'b0), .pin11(H5), .pin12(1'b0),
    .pin13(1'b0), .pin14(H6), .pin15(1'b1), .pin16(1'b1));
  _7485 _7485_9 (
    .pin1(1'b0), .pin2(_7485_8_pin7), .pin3(_7485_8_pin6), .pin4(_7485_8_pin5), .pin7(_7400_1_pin4),
    .pin8(1'b0), .pin9(H8), .pin10(1'b0), .pin11(H9), .pin12(1'b1), .pin13(1'b0), .pin14(1'b0), .pin15(1'b0),
    .pin16(1'b1));  // open: pin5, pin6
  _7485 _7485_10 (
    .pin1(H3), .pin2(1'b0), .pin3(1'b1), .pin4(1'b0), .pin5(_7485_10_pin5), .pin6(_7485_10_pin6),
    .pin7(_7485_10_pin7), .pin8(1'b0), .pin9(H0), .pin10(1'b0), .pin11(H1), .pin12(1'b0), .pin13(1'b0),
    .pin14(H2), .pin15(1'b0), .pin16(1'b1));
  _7485 _7485_11 (
    .pin1(H7), .pin2(_7485_10_pin7), .pin3(_7485_10_pin6), .pin4(_7485_10_pin5), .pin5(_7485_11_pin5),
    .pin6(_7485_11_pin6), .pin7(_7485_11_pin7), .pin8(1'b0), .pin9(H4), .pin10(1'b1), .pin11(H5),
    .pin12(1'b1), .pin13(1'b1), .pin14(H6), .pin15(1'b1), .pin16(1'b1));
  _7485 _7485_12 (
    .pin1(1'b0), .pin2(_7485_11_pin7), .pin3(_7485_11_pin6), .pin4(_7485_11_pin5), .pin5(_7400_1_pin5),
    .pin8(1'b0), .pin9(H8), .pin10(1'b0), .pin11(H9), .pin12(1'b1), .pin13(1'b0), .pin14(1'b0), .pin15(1'b0),
    .pin16(1'b1));  // open: pin6, pin7

  // Other names for the same wires on the sheet: HCOUNT[9:0] = {H9, H8, H7, H6, H5, H4, H3, H2, H1, H0};
  //   VCOUNT[9:0] = {V9, V8, V7, V6, V5, V4, V3, V2, V1, V0}

  // Notes on the sheet:
  //   Master_VGA_Clock: Hz: 25175000
  //   Test_Clock: Hz: 10000
  //   COUNTERS
  //   I/O SUITE
  //   CLR
  //   VGA DRIVER
  //   SYNC GEN
endmodule
